# Fritzing sketch Montage coeur 2 (saved by Fritzing 0.9.3b)
breadboards: 1

parts:
  LED1 = LED - 5mm [color="Red (633nm)" package="5 mm [THT]"]
  LED2 = LED - 5mm [color="Red (633nm)" package="5 mm [THT]"]
  LED3 = LED - 5mm [color="Red (633nm)" package="5 mm [THT]"]
  LED4 = LED - 5mm [color="Red (633nm)" package="5 mm [THT]"]
  LED5 = LED - 5mm [color="Red (633nm)" package="5 mm [THT]"]
  LED6 = LED - 5mm [color="Red (633nm)" package="5 mm [THT]"]
  LED7 = LED - 5mm [color="Red (633nm)" package="5 mm [THT]"]
  LED8 = LED - 5mm [color="Red (633nm)" package="5 mm [THT]"]
  LED9 = LED - 5mm [color="Red (633nm)" package="5 mm [THT]"]
  LED10 = LED - 5mm [color="Red (633nm)" package="5 mm [THT]"]
  R1 = Resistor [tolerance=±5% resistance=220 package=THT]
  R2 = Resistor [tolerance=±5% resistance=220 package=THT]
  R3 = Resistor [tolerance=±5% resistance=220 package=THT]
  R4 = Resistor [tolerance=±5% resistance=220 package=THT]
  R5 = Resistor [tolerance=±5% resistance=220 package=THT]
  R6 = Resistor [tolerance=±5% resistance=220 package=THT]
  R7 = Resistor [tolerance=±5% resistance=220 package=THT]
  R8 = Resistor [tolerance=±5% resistance=220 package=THT]
  R9 = Resistor [tolerance=±5% resistance=220 package=THT]
  Composant1 = Arduino Uno (Rev3)
  R10 = Resistor [tolerance=±5% resistance=220 package=THT]

nets:
  N1: LED1.cathode, LED2.cathode, LED3.cathode, LED4.cathode, LED5.cathode, LED6.cathode, LED7.cathode, LED8.cathode, LED9.cathode, LED10.cathode, Composant1.GND
  N2: LED1.anode, R10.Pin_1
  N3: LED2.anode, R7.Pin_1
  N4: LED3.anode, R8.Pin_1
  N5: LED4.anode, R9.Pin_1
  N6: LED5.anode, R2.Pin_1
  N7: LED6.anode, R1.Pin_1
  N8: LED7.anode, R3.Pin_1
  N9: LED8.anode, R4.Pin_1
  N10: LED9.anode, R5.Pin_1
  N11: R1.Pin_0, Composant1.D8
  N12: R2.Pin_0, Composant1.D9_PWM
  N13: R3.Pin_0, Composant1.D7
  N14: R4.Pin_0, Composant1.D6_PWM
  N15: R5.Pin_0, Composant1.D5_PWM
  N16: R6.Pin_0, Composant1.D4
  N17: R7.Pin_0, Composant1.D3_PWM
  N18: R8.Pin_0, Composant1.D2
  N19: R9.Pin_0, Composant1.D10_PWM/SS
  N20: Composant1.D11_PWM/MOSI, R10.Pin_0
