# Fritzing sketch Montage coeur (saved by Fritzing 0.9.3b)
breadboards: 1

parts:
  LED1 = LED - 5mm [color="Red (633nm)" package="5 mm [THT]"]
  LED2 = LED - 5mm [color="Red (633nm)" package="5 mm [THT]"]
  LED3 = LED - 5mm [color="Red (633nm)" package="5 mm [THT]"]
  LED4 = LED - 5mm [color="Red (633nm)" package="5 mm [THT]"]
  LED5 = LED - 5mm [color="Red (633nm)" package="5 mm [THT]"]
  LED6 = LED - 5mm [color="Red (633nm)" package="5 mm [THT]"]
  LED7 = LED - 5mm [color="Red (633nm)" package="5 mm [THT]"]
  LED10 = LED - 5mm [color="Red (633nm)" package="5 mm [THT]"]
  LED12 = LED - 5mm [color="Red (633nm)" package="5 mm [THT]"]
  Composant1 = Arduino Uno (Rev3)
  LED14 = LED - 5mm [color="Red (633nm)" package="5 mm [THT]"]

nets:
  N1: LED1.cathode, Composant1.D10_PWM/SS
  N2: LED1.anode, LED2.cathode, LED3.anode, LED4.cathode, LED5.cathode, LED6.anode, LED10.anode, LED12.anode, Composant1.GND, LED14.cathode
  N3: LED2.anode, Composant1.D9_PWM
  N4: LED3.cathode, Composant1.D6_PWM
  N5: LED4.anode, Composant1.D3_PWM
  N6: LED5.anode, Composant1.D2
  N7: LED6.cathode, LED7.anode, Composant1.D12/MISO
  N8: LED7.cathode, Composant1.D13/SCK
  N9: LED10.cathode, Composant1.D7
  N10: LED12.cathode, Composant1.D11_PWM/MOSI
  N11: Composant1.D5_PWM, LED14.anode
